# Fritzing sketch escape_game_circuit_search_schematic (saved by Fritzing 0.9.6b)
breadboards: 1

parts:
  Part1 = Arduino Uno (Rev3)
  R1 = Resistor [tolerance=±5% power=0.25 resistance=220 package=THT]
  R2 = Resistor [tolerance=±5% power=0.25 resistance=1k package=THT]
  R3 = Resistor [tolerance=±5% power=0.25 resistance=220 package=THT]
  LED2 = LED - 5mm [color="Blue (505nm)" current=0.030 package="5 mm [THT]"]
  LED4 = LED - 5mm [color="Red (635nm)" current=0.030 package="5 mm [THT]"]
  LED5 = LED - 5mm [color="Yellow (585nm)" current=0.030 package="5 mm [THT]"]
  R4 = Resistor [tolerance=±5% power=0.25 resistance=1k package=THT]
  R5 = Resistor [tolerance=±5% power=0.25 resistance=1k package=THT]
  R6 = Resistor [tolerance=±5% power=0.25 resistance=10k package=THT]
  R7 = Resistor [tolerance=±5% power=0.25 resistance=10k package=THT]
  R8 = Resistor [tolerance=±5% power=0.25 resistance=100k package=THT]
  R9 = Resistor [tolerance=±5% power=0.25 resistance=100k package=THT]
  J1 = Piezo Speaker [part_number=PKM22EPP-40]
  R10 = Resistor [tolerance=±5% power=0.25 resistance=100 package=THT]

nets:
  N1: Part1.A0, R8.Pin_0, R9.Pin_1
  N2: Part1.A1, R6.Pin_0, R7.Pin_1
  N3: Part1.A2, R4.Pin_0, R5.Pin_1
  N4: Part1.D12/MISO, R10.Pin_0
  N5: Part1.GND, LED2.cathode, LED4.cathode, LED5.cathode, R5.Pin_0, R7.Pin_0, R9.Pin_0, J1.pin2
  N6: Part1.D2, R1.Pin_0
  N7: Part1.D3_PWM, R2.Pin_0
  N8: Part1.D4, R3.Pin_0
  N9: Part1.5V, R4.Pin_1, R6.Pin_1, R8.Pin_1
  N10: R1.Pin_1, LED4.anode
  N11: R2.Pin_1, LED2.anode
  N12: R3.Pin_1, LED5.anode
  N13: J1.pin1, R10.Pin_1
